# Fritzing sketch 3raAyudaSketch (saved by Fritzing 0.9.3b)
breadboards: 1

parts:
  U1 = ESP32S-HiLetgo [part_number=ESP32S-HiLetgo]
  M1 = DC Motor
  Grove1 = Grove OLED 128x96
  Part1 = InvenSense MPU6050

nets:
  GND: U1.GPIO11, M1.pin_2, Grove1.GND, Part1.GND
  VCC: U1.VIN, Grove1.VCC, Part1.VCC
  N1: U1.GPIO5, M1.pin_1
  N2: U1.GPIO21, Grove1.SDA, Part1.SDA
  N3: U1.GPIO23, Grove1.SCL, Part1.SCL

custom parts:
  ESP32S-HiLetgo: HiLetgo ESP-WROOM-32 ESP32 ESP-32S Development Board 2.4GHz Dual-Mode WiFi + Bluetooth Dual Cores Microcontroller The ESP32 integrated with Antenna switches, RF Balun, power amplifiers, low-noise amplifiers, filters, and management modules, and the entire solution occupies the least area of PCB. 2.4 GHz Wi-Fi plus Bluetooth dual-mode chip, with TSMC Ultra-low power consumption 40nm technology,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
